# Fritzing sketch Fritz_final (saved by Fritzing 0.9.3b)
breadboards: 1

parts:
  Part1 = Arduino Uno (Rev3)
  R1 = Resistor [tolerance=±5% resistance=220 package=THT]
  LED1 = LED - 5mm [color="Red (633nm)" package="5 mm [THT]"]
  LED2 = LED - 5mm [color="Green (565nm)" package="5 mm [THT]"]
  LED3 = LED - 5mm [color="Yellow (592nm)" package="5 mm [THT]"]
  R2 = Resistor [tolerance=±5% resistance=220 package=THT]
  R3 = Resistor [tolerance=±5% resistance=220 package=THT]
  hc-sr1 = hc-sr04

nets:
  GND: Part1.GND, LED1.anode, LED2.anode, LED3.anode, hc-sr1.GND
  N1: Part1.AREF, R1.Pin_0
  N2: Part1.D6_PWM, R3.Pin_0, hc-sr1.Echo
  N3: Part1.D7, R2.Pin_0, hc-sr1.Trig
  5V: Part1.5V, hc-sr1.VCC
  N4: R1.Pin_1, LED2.cathode
  N5: LED1.cathode, R2.Pin_1
  N6: LED3.cathode, R3.Pin_1
